// Logisim project ALU.circ as structural Verilog: 1 circuit, main circuit main
module main (
  input  [7:0] Operand1,
  input  [7:0] Operand2,
  input  [2:0] _3BitSelectInput,
  output [7:0] Result
);

  wire [7:0] adder_1_out, and_1_out, not_1_out, or_1_out, subtractor_1_out;

  Adder adder_1 (.a(Operand2), .b(Operand1), .out(adder_1_out));  // open: cin, cout
  Subtractor subtractor_1 (.a(Operand2), .b(Operand1), .out(subtractor_1_out));  // open: bin, bout
  assign and_1_out = Operand1 & Operand2;  // AND_Gate and_1, 8 bits wide
  Multiplexer #(.select(3), .width(8), .enable("false")) multiplexer_1 (
    .in0(adder_1_out), .in1(subtractor_1_out), .in2(and_1_out), .in3(or_1_out), .in4(not_1_out),
    .out(Result), .sel(_3BitSelectInput));  // open: in5, in6, in7
  assign not_1_out = ~Operand1;  // NOT_Gate not_1, 8 bits wide
  assign or_1_out = Operand1 | Operand2;  // OR_Gate or_1, 8 bits wide
endmodule
