// Logisim project CPUcircuit.circ as structural Verilog: 1 circuit, main circuit main
module main (
  input  IP_Reset,
  input  in_2,
  output [7:0] Output_Cell
);

  wire clock_1_out, decoder_1_out0, decoder_1_out1, decoder_1_out2, decoder_1_out3, decoder_2_out0,
       decoder_2_out1, decoder_2_out2, decoder_2_out3, main_1_formatbit, main_1_readram, main_1_resetexec,
       main_1_startexecutionunit, main_2_destonop2bus, main_2_done, main_2_outputpin, main_2_resultcapture,
       main_2_resulttobus, main_2_src_op1onbus, main_2_writeregenable;
  wire [1:0] main_1_destregbit0, main_1_srcregbit0;
  wire [2:0] main_1_opcodebit0, main_2_alumodebits;
  wire [7:0] ALU_result, controlled_buffer_1_out, controlled_buffer_2_out, main_1_addressbus,
       main_1_immediatevalue, multiplexer_1_out, multiplexer_2_out, multiplexer_3_out, ram_1_data,
       register_2_q, WR_q, XR_q, YR_q, ZR_q;

  Clock clock_1 (.out(clock_1_out));
  Multiplexer #(.width(8), .enable("false")) multiplexer_1 (
    .in0(multiplexer_2_out), .in1(main_1_immediatevalue), .out(multiplexer_1_out), .sel(main_1_formatbit));
  Multiplexer #(.select(2), .width(8), .enable("false")) multiplexer_2 (
    .in0(WR_q), .in1(XR_q), .in2(YR_q), .in3(ZR_q), .out(multiplexer_2_out), .sel(main_1_srcregbit0));
  FullFetchUnit_main main_1 (
    .ResetIP(IP_Reset), .CLOCK(clock_1_out), .Start(in_2), .DoneSignal(main_2_done),
    .OpcodeBit2(main_1_opcodebit0[2]), .OpcodeBit1(main_1_opcodebit0[1]), .OpcodeBit0(main_1_opcodebit0[0]),
    .DestRegBit1(main_1_destregbit0[1]), .DestRegBit0(main_1_destregbit0[0]),
    .SrcRegBit1(main_1_srcregbit0[1]), .SrcRegBit0(main_1_srcregbit0[0]), .FormatBit(main_1_formatbit),
    .ResetExec(main_1_resetexec), .AddressBus(main_1_addressbus), .ReadRAM(main_1_readram),
    .StartExecutionUnit(main_1_startexecutionunit), .ImmediateValue(main_1_immediatevalue),
    .DataBus(ram_1_data));
  assign controlled_buffer_1_out = main_2_src_op1onbus ? multiplexer_1_out : 8'bz;  // Controlled_Buffer controlled_buffer_1
  Multiplexer #(.select(2), .width(8), .disabled(0), .enable("false")) multiplexer_3 (
    .in0(WR_q), .in1(XR_q), .in2(YR_q), .in3(ZR_q), .out(multiplexer_3_out), .sel(main_1_destregbit0));
  Register register_1 (
    .D(multiplexer_3_out), .en(main_2_outputpin), .Q(Output_Cell), .clk(main_2_outputpin));  // open: clr
  ExecutionUnit_main main_2 (
    .Reset(main_1_resetexec), .CLK(clock_1_out), .StartExec(main_1_startexecutionunit),
    .Opcode(main_1_opcodebit0), .Src_OP1onBus(main_2_src_op1onbus), .ALUModeBits(main_2_alumodebits),
    .DestOnOP2Bus(main_2_destonop2bus), .ResultCapture(main_2_resultcapture),
    .ResultToBus(main_2_resulttobus), .WriteRegEnable(main_2_writeregenable), .Done(main_2_done),
    .OutPutPin(main_2_outputpin));
  Decoder #(.select(2), .disabled(0)) decoder_1 (
    .out0(decoder_1_out0), .out1(decoder_1_out1), .out2(decoder_1_out2), .out3(decoder_1_out3),
    .sel(main_1_destregbit0), .en(main_2_destonop2bus));
  assign controlled_buffer_2_out = decoder_1_out1 ? XR_q : 8'bz;  // Controlled_Buffer controlled_buffer_2
  assign controlled_buffer_2_out = decoder_1_out0 ? WR_q : 8'bz;  // Controlled_Buffer controlled_buffer_3
  Decoder #(.select(2), .disabled(0)) decoder_2 (
    .out0(decoder_2_out0), .out1(decoder_2_out1), .out2(decoder_2_out2), .out3(decoder_2_out3),
    .sel(main_1_destregbit0), .en(main_2_writeregenable));
  assign controlled_buffer_2_out = decoder_1_out2 ? YR_q : 8'bz;  // Controlled_Buffer controlled_buffer_4
  assign controlled_buffer_2_out = decoder_1_out3 ? ZR_q : 8'bz;  // Controlled_Buffer controlled_buffer_5
  Register WR (.D(controlled_buffer_1_out), .en(decoder_2_out0), .Q(WR_q), .clk(clock_1_out));  // open: clr
  Register XR (.D(controlled_buffer_1_out), .en(decoder_2_out1), .Q(XR_q), .clk(clock_1_out));  // open: clr
  Register YR (.D(controlled_buffer_1_out), .en(decoder_2_out2), .Q(YR_q), .clk(clock_1_out));  // open: clr
  Register ZR (.D(controlled_buffer_1_out), .en(decoder_2_out3), .Q(ZR_q), .clk(clock_1_out));  // open: clr
  ALU_main ALU (
    ._3BitSelectInput(main_2_alumodebits), .Operand1(controlled_buffer_1_out),
    .Operand2(controlled_buffer_2_out), .Result(ALU_result));
  RAM ram_1 (
    .addr(main_1_addressbus), .data(ram_1_data), .sel(1'b1), .clk(clock_1_out), .ld(main_1_readram));  // open: clr
  Register #(.trigger("high")) register_2 (
    .D(ALU_result), .en(main_2_resultcapture), .Q(register_2_q), .clk(main_2_resultcapture));  // open: clr
  assign controlled_buffer_1_out = main_2_resulttobus ? register_2_q : 8'bz;  // Controlled_Buffer controlled_buffer_6
endmodule
