// Logisim project ExecutionUnit.circ as structural Verilog: 1 circuit, main circuit main
module main (
  input  Reset,
  input  CLK,
  input  StartExec,
  input  [2:0] Opcode,
  output Src_OP1onBus,
  output [2:0] ALUModeBits,
  output DestOnOP2Bus,
  output ResultCapture,
  output ResultToBus,
  output WriteRegEnable,
  output Done,
  output OutPutPin
);

  wire _0, _1, _2, _3, _4, _5, _6, decoder_1_out0, decoder_1_out1, decoder_1_out2, decoder_1_out3,
       decoder_1_out4, decoder_1_out5, decoder_1_out6, main_1_src_op1onbus, main_1_writetoregenable,
       main_2_destonop2bus, main_2_resultcapture, main_2_resulttobus, main_2_src_op1onbus,
       main_2_writeregenable, main_3_destonop2bus, main_3_resultcapture, main_3_resulttobus,
       main_3_src_op1onbus, main_3_writeregenable, main_4_destonop2bus, main_4_resultcapture,
       main_4_resulttobus, main_4_src_op1onbus, main_4_writeregenable, main_5_destonop2bus,
       main_5_resultcapture, main_5_resulttobus, main_5_src_op1onbus, main_5_writeregenable,
       main_6_destonop2bus, main_6_resultcapture, main_6_resulttobus, main_6_src_op1onbus,
       main_6_writeregenable;
  wire [2:0] main_2_alumodebits, main_3_alumodebits, main_4_alumodebits, main_5_alumodebits,
       main_6_alumodebits;

  Decoder #(.select(3), .disabled(0)) decoder_1 (
    .out0(decoder_1_out0), .out1(decoder_1_out1), .out2(decoder_1_out2), .out3(decoder_1_out3),
    .out4(decoder_1_out4), .out5(decoder_1_out5), .out6(decoder_1_out6), .sel(Opcode), .en(StartExec));  // open: out7
  MOV_EU_main main_1 (
    .Reset(Reset), .CLK(CLK), .E(decoder_1_out0), .Src_Op1OnBus(main_1_src_op1onbus),
    .WriteToRegEnable(main_1_writetoregenable), .Done(_0));
  ADD_main main_2 (
    .Reset(Reset), .CLK(CLK), .E(decoder_1_out1), .ALUModeBits(main_2_alumodebits),
    .Src_Op1OnBus(main_2_src_op1onbus), .DestOnOp2Bus(main_2_destonop2bus),
    .ResultCapture(main_2_resultcapture), .ResultToBus(main_2_resulttobus),
    .WriteRegEnable(main_2_writeregenable), .Done(_1));
  SUB_main main_3 (
    .Reset(Reset), .CLK(CLK), .E(decoder_1_out2), .ALUModeBits(main_3_alumodebits),
    .Src_Op1OnBus(main_3_src_op1onbus), .DestOnOp2Bus(main_3_destonop2bus),
    .ResultCapture(main_3_resultcapture), .ResultToBus(main_3_resulttobus),
    .WriteRegEnable(main_3_writeregenable), .Done(_2));
  AND_main main_4 (
    .Reset(Reset), .CLK(CLK), .E(decoder_1_out3), .ALUModeBits(main_4_alumodebits),
    .Src_Op1OnBus(main_4_src_op1onbus), .DestOnOp2Bus(main_4_destonop2bus),
    .ResultCapture(main_4_resultcapture), .ResultToBus(main_4_resulttobus),
    .WriteRegEnable(main_4_writeregenable), .Done(_3));
  OR_main main_5 (
    .Reset(Reset), .CLK(CLK), .E(decoder_1_out4), .ALUModeBits(main_5_alumodebits),
    .Src_Op1OnBus(main_5_src_op1onbus), .DestOnOp2Bus(main_5_destonop2bus),
    .ResultCapture(main_5_resultcapture), .ResultToBus(main_5_resulttobus),
    .WriteRegEnable(main_5_writeregenable), .Done(_4));
  NOT_main main_6 (
    .Reset(Reset), .CLK(CLK), .E(decoder_1_out5), .ALUModeBits(main_6_alumodebits),
    .Src_Op1OnBus(main_6_src_op1onbus), .DestOnOp2Bus(main_6_destonop2bus),
    .ResultCapture(main_6_resultcapture), .ResultToBus(main_6_resulttobus),
    .WriteRegEnable(main_6_writeregenable), .Done(_5));
  OUT_main main_7 (.CLK(CLK), .RESET(Reset), .E(decoder_1_out6), .Outpin(OutPutPin), .Done(_6));
  or or_1 (Src_OP1onBus, main_1_src_op1onbus, main_2_src_op1onbus, main_3_src_op1onbus, main_4_src_op1onbus, main_5_src_op1onbus, main_6_src_op1onbus);
  assign ALUModeBits = main_2_alumodebits | main_3_alumodebits | main_4_alumodebits | main_5_alumodebits | main_6_alumodebits;  // OR_Gate or_2, 3 bits wide
  or or_3 (DestOnOP2Bus, main_2_destonop2bus, main_3_destonop2bus, main_4_destonop2bus, main_5_destonop2bus, main_6_destonop2bus);
  or or_4 (ResultCapture, main_2_resultcapture, main_3_resultcapture, main_4_resultcapture, main_5_resultcapture, main_6_resultcapture);
  or or_5 (ResultToBus, main_2_resulttobus, main_3_resulttobus, main_4_resulttobus, main_5_resulttobus, main_6_resulttobus);
  or or_6 (WriteRegEnable, main_1_writetoregenable, main_2_writeregenable, main_3_writeregenable, main_4_writeregenable, main_5_writeregenable, main_6_writeregenable);
  or or_7 (Done, _0, _1, _2, _3, _4, _5, _6);
endmodule
