// Logisim project FetchUnit.circ as structural Verilog: 1 circuit, main circuit main
module main (
  input  F_fmt_bit,
  input  D_Done_Signal,
  input  CLK,
  output ResetExecUnit,
  output ReadLine,
  output IPLatch,
  output IncIP,
  output StartExec,
  output Demux
);

  wire and_1_out, and_2_out, and_3_out, and_4_out, and_5_out, nor_1_out, or_1_out, or_2_out, S0_q, S1_q, S2_q;

  and and_1 (and_1_out, ~S2_q, ~S1_q, S0_q, ~F_fmt_bit);  // AND_Gate
  and and_2 (and_2_out, ~S2_q, S1_q, S0_q);  // AND_Gate
  and and_3 (and_3_out, S2_q, ~S1_q, ~S0_q, ~D_Done_Signal);  // AND_Gate
  and and_4 (and_4_out, ~S2_q, ~S1_q, S0_q, F_fmt_bit);  // AND_Gate
  and and_5 (and_5_out, ~S2_q, S1_q, ~S0_q);  // AND_Gate
  or or_1 (or_1_out, and_1_out, and_2_out, and_3_out);
  or or_2 (or_2_out, and_4_out, and_5_out);
  nor nor_1 (nor_1_out, S2_q, S0_q);
  D_Flip_Flop S2 (.clk(CLK), .D(or_1_out), .Q(S2_q), .en(CLK));  // open: Qn, preset, reset
  D_Flip_Flop S1 (.clk(CLK), .D(or_2_out), .Q(S1_q), .en(CLK));  // open: Qn, preset, reset
  D_Flip_Flop S0 (.clk(CLK), .D(nor_1_out), .Q(S0_q), .en(CLK));  // open: Qn, preset, reset
  nor nor_2 (ResetExecUnit, S2_q, S1_q, S0_q);
  nor nor_3 (IncIP, S2_q, S0_q);
  and and_6 (StartExec, S2_q, ~S1_q, ~S0_q);  // AND_Gate
  and and_7 (Demux, ~S2_q, S1_q, ~S0_q);  // AND_Gate

  assign IPLatch = IncIP;
  assign ReadLine = IncIP;
endmodule
