// Logisim project FullFetchUnit.circ as structural Verilog: 1 circuit, main circuit main
module main (
  input  ResetIP,
  input  CLOCK,
  input  Start,
  input  DoneSignal,
  input  [7:0] DataBus,
  output ResetExec,
  output [7:0] AddressBus,
  output ReadRAM,
  output StartExecutionUnit,
  output [7:0] ImmediateValue,
  output OpcodeBit2,
  output OpcodeBit1,
  output OpcodeBit0,
  output DestRegBit1,
  output DestRegBit0,
  output SrcRegBit1,
  output SrcRegBit0,
  output FormatBit
);

  wire and_1_out, main_1_demux, main_1_incip, main_1_iplatch, not_1_out, not_2_out;
  wire [7:0] counter_1_q, demultiplexer_1_out0, demultiplexer_1_out1;

  Register Instruction_register (
    .D(demultiplexer_1_out0), .en(not_1_out),
    .Q({OpcodeBit2, OpcodeBit1, OpcodeBit0, DestRegBit1, DestRegBit0, SrcRegBit1, SrcRegBit0, FormatBit}),
    .clk(and_1_out));  // open: clr
  and and_1 (and_1_out, CLOCK, Start);
  not not_1 (not_1_out, main_1_demux);
  FetchUnit_main main_1 (
    .F_fmt_bit(FormatBit), .D_Done_Signal(DoneSignal), .CLK(and_1_out), .ResetExecUnit(ResetExec),
    .ReadLine(ReadRAM), .IPLatch(main_1_iplatch), .IncIP(main_1_incip), .StartExec(StartExecutionUnit),
    .Demux(main_1_demux));
  Register register_1 (.D(demultiplexer_1_out1), .en(main_1_demux), .Q(ImmediateValue), .clk(and_1_out));  // open: clr
  Demultiplexer #(.width(8), .enable("false")) demultiplexer_1 (
    .out0(demultiplexer_1_out0), .out1(demultiplexer_1_out1), .in(DataBus), .sel(main_1_demux));
  not not_2 (not_2_out, main_1_incip);
  Counter #(.trigger("falling")) counter_1 (
    .count(main_1_incip), .Q(counter_1_q), .clk(not_2_out), .clr(ResetIP));  // open: load, D, carry
  assign AddressBus = main_1_iplatch ? counter_1_q : 8'bz;  // Controlled_Buffer controlled_buffer_1
endmodule
