// Logisim project MOV-EU.circ as structural Verilog: 1 circuit, main circuit main
module main (
  input  Reset,
  input  CLK,
  input  E,
  output Src_Op1OnBus,
  output WriteToRegEnable,
  output Done
);

  wire and_1_out, or_1_out, S0_q, S0_qn, S1_q, S1_qn, xor_1_out;

  xor xor_1 (xor_1_out, S1_q, S0_q);
  or or_1 (or_1_out, S1_q, E);
  and and_1 (and_1_out, or_1_out, S0_qn);
  D_Flip_Flop S1 (.clk(CLK), .D(xor_1_out), .Q(S1_q), .Qn(S1_qn), .en(CLK), .reset(Reset));  // open: preset
  D_Flip_Flop S0 (.clk(CLK), .D(and_1_out), .Q(S0_q), .Qn(S0_qn), .en(CLK), .reset(Reset));  // open: preset
  and and_2 (Src_Op1OnBus, S1_qn, S0_q);
  and and_3 (Done, S1_q, S0_qn);

  assign WriteToRegEnable = Src_Op1OnBus;
endmodule
