// Logisim project NOT.circ as structural Verilog: 1 circuit, main circuit main
module main (
  input  Reset,
  input  CLK,
  input  E,
  output [2:0] ALUModeBits,
  output Src_Op1OnBus,
  output DestOnOp2Bus,
  output ResultCapture,
  output ResultToBus,
  output WriteRegEnable,
  output Done
);

  wire and_1_out, or_1_out, S0_q, S0_qn, S1_q, S1_qn, xor_1_out;

  xor xor_1 (xor_1_out, S1_q, S0_q);
  or or_1 (or_1_out, S1_q, E);
  and and_1 (and_1_out, or_1_out, S0_qn);
  D_Flip_Flop S1 (.clk(CLK), .D(xor_1_out), .Q(S1_q), .Qn(S1_qn), .en(CLK), .reset(Reset));  // open: preset
  D_Flip_Flop S0 (.clk(CLK), .D(and_1_out), .Q(S0_q), .Qn(S0_qn), .en(CLK), .reset(Reset));  // open: preset
  Multiplexer #(.width(3), .disabled(0), .enable("false")) multiplexer_1 (
    .in0(3'b000), .in1(3'b100), .out(ALUModeBits), .sel(E));
  and State_01 (DestOnOp2Bus, S1_qn, S0_q);
  and State_10 (ResultToBus, S0_qn, S1_q);
  and State_11 (Done, S1_q, S0_q);

  assign ResultCapture = DestOnOp2Bus;
  assign Src_Op1OnBus = DestOnOp2Bus;
  assign WriteRegEnable = ResultToBus;
endmodule
