// Logisim project OUT.circ as structural Verilog: 1 circuit, main circuit main
module main (
  input  CLK,
  input  RESET,
  input  E,
  output Outpin,
  output Done
);

  wire and_1_out, or_1_out, S0_q, S0_qn, S1_q, S1_qn, xor_1_out;

  or or_1 (or_1_out, S1_q, E);
  xor xor_1 (xor_1_out, S1_q, S0_q);
  and and_1 (and_1_out, S0_qn, or_1_out);
  D_Flip_Flop S1 (.clk(CLK), .D(xor_1_out), .Q(S1_q), .Qn(S1_qn), .en(CLK), .reset(RESET));  // open: preset
  D_Flip_Flop S0 (.clk(CLK), .D(and_1_out), .Q(S0_q), .Qn(S0_qn), .en(CLK), .reset(RESET));  // open: preset
  and and_2 (Outpin, S1_qn, S0_q);
  and and_3 (Done, S1_q, S0_qn);
endmodule
